# Fritzing sketch plant-moisture (saved by Fritzing 0.9.3b)
breadboards: 1

parts:
  U1 = NodeMCU V1.0
  LCD_20x4_I2C1 = Grove OLED 128x96
  Soil_Moisture_Sensor = Soil Moisture Sensor
  microUSB = USB Connectors [package=usb-microb]
  BL-5CT_3_7V_1050mAh = LIPO-1000mAh [package=lipo-1000]
  BL-5CT_3_7V_1050mAh_2 = LIPO-1000mAh [package=lipo-1000]
  TP4056_Li-Pol_Charger_3_7V_1S = TP4056 [chip_label=TP4056 package="DIP (Dual Inline) [THT]"]
  TP4056_Li-Pol_Charger_3_7V_1S_2 = TP4056 [chip_label=TP4056 package="DIP (Dual Inline) [THT]"]
  Water_Pump_3-12V = DC Motor  # not connected
  U3V12F5_-_step-up_voltage_regulator_5V_1_4A = Voltage Regulator [package=v-reg_dpack]
  U3V12F5_-_step-up_voltage_regulator_5V_1_4A_2 = Voltage Regulator [package=v-reg_dpack]

nets:
  N1: U1.D1, LCD_20x4_I2C1.SCL
  N2: U1.D2, LCD_20x4_I2C1.SDA
  3V3: U1.3V3, Soil_Moisture_Sensor.VCC
  GND: U1.GND, Soil_Moisture_Sensor.GND
  N3: U1.RSV#40, LCD_20x4_I2C1.VCC
  N4: U1.RSV#41, LCD_20x4_I2C1.GND
  N5: U1.A0, Soil_Moisture_Sensor.SIG
  N6: microUSB.D+, TP4056_Li-Pol_Charger_3_7V_1S.pin1, TP4056_Li-Pol_Charger_3_7V_1S_2.pin1
  N7: microUSB.GND, TP4056_Li-Pol_Charger_3_7V_1S.pin2, TP4056_Li-Pol_Charger_3_7V_1S_2.pin2
  N8: BL-5CT_3_7V_1050mAh.+, TP4056_Li-Pol_Charger_3_7V_1S.pin5
  N9: BL-5CT_3_7V_1050mAh.-, TP4056_Li-Pol_Charger_3_7V_1S.pin4
  N10: BL-5CT_3_7V_1050mAh_2.+, TP4056_Li-Pol_Charger_3_7V_1S_2.pin5
  N11: BL-5CT_3_7V_1050mAh_2.-, TP4056_Li-Pol_Charger_3_7V_1S_2.pin4
  N12: TP4056_Li-Pol_Charger_3_7V_1S.pin3, U3V12F5_-_step-up_voltage_regulator_5V_1_4A.IN
  N13: TP4056_Li-Pol_Charger_3_7V_1S.pin6, U3V12F5_-_step-up_voltage_regulator_5V_1_4A.ADJ
  N14: TP4056_Li-Pol_Charger_3_7V_1S_2.pin3, U3V12F5_-_step-up_voltage_regulator_5V_1_4A_2.IN
  N15: TP4056_Li-Pol_Charger_3_7V_1S_2.pin6, U3V12F5_-_step-up_voltage_regulator_5V_1_4A_2.ADJ

custom parts:
  NodeMCU V1.0: ESP8266 based NodeMCU
  TP4056: A DIP stand-in part for whatever IC you want. With 6 pins on a 300mil dual inline package (DIP) footprint.
